# Fritzing sketch wiring (saved by Fritzing 0.9.3b)

parts:
  Raspberry_Pi1 = Raspberry Pi 2
  X1 = DB9 Connector [package=db9]
  X2 = DB9 Connector [package=db9]
  R11 = Resistor [tolerance=±5% resistance=330 package=THT]
  R7 = Resistor [tolerance=±5% resistance=330 package=THT]
  R8 = Resistor [tolerance=±5% resistance=330 package=THT]
  R9 = Resistor [tolerance=±5% resistance=330 package=THT]
  R10 = Resistor [tolerance=±5% resistance=330 package=THT]
  R1 = Resistor [tolerance=±5% resistance=330 package=THT]
  R2 = Resistor [tolerance=±5% resistance=330 package=THT]
  R3 = Resistor [tolerance=±5% resistance=330 package=THT]
  R4 = Resistor [tolerance=±5% resistance=330 package=THT]
  R6 = Resistor [tolerance=±5% resistance=330 package=THT]
  R5 = Resistor [tolerance=±5% resistance=330 package=THT]

nets:
  N1: Raspberry_Pi1.ID_SD, R1.Pin_0
  N2: Raspberry_Pi1.GIPO5, R2.Pin_0
  N3: Raspberry_Pi1.GIPO6, R3.Pin_0
  N4: Raspberry_Pi1.GIPO13, R4.Pin_0
  N5: Raspberry_Pi1.GIPO19, R5.Pin_1
  N6: Raspberry_Pi1.GIPO26, R6.Pin_1
  N7: Raspberry_Pi1.GND, X1.8, X2.8
  N8: Raspberry_Pi1.GIPO16, R11.Pin_1
  N9: Raspberry_Pi1.ID_SC, R10.Pin_0
  N10: Raspberry_Pi1.GIPO7, R9.Pin_0
  N11: Raspberry_Pi1.GIPO8, R8.Pin_0
  N12: Raspberry_Pi1.GIPO25, R7.Pin_0
  N13: X1.1, R7.Pin_1
  N14: X1.2, R8.Pin_1
  N15: X1.3, R9.Pin_1
  N16: X1.4, R10.Pin_1
  N17: X1.6, R11.Pin_0
  N18: X2.1, R1.Pin_1
  N19: X2.2, R2.Pin_1
  N20: X2.3, R3.Pin_1
  N21: X2.4, R4.Pin_1
  N22: X2.6, R5.Pin_0
  N23: X2.9, R6.Pin_0
